# Fritzing sketch Diagrama Conexiones (saved by Fritzing 0.9.3b)
breadboards: 1

parts:
  S1 = H-Bridge with L298N
  J1 = Basic Servo
  ULTRASONIDO = hc-sr04
  BAT1 = BC9VPC [package=bc9vpc]
  SWITCH = SWITCH_SPDT [package=kps-1290]
  M1 = DC Motor
  Componente1 = Arduino Uno (Rev3) - ICSP
  M2 = DC Motor
  TCTR5000 = TCRT5000 sensor module [part_number=151608]
  TCRT5000 = TCRT5000 sensor module

nets:
  N1: S1.12V, SWITCH.P
  GND: S1.GND, J1.gnd, ULTRASONIDO.GND, BAT1.V-, Componente1.GND, TCTR5000.T-
  VCC: S1.5V, J1.vcc, ULTRASONIDO.VCC, Componente1.VIN, TCTR5000.T+, TCRT5000.T+
  N2: S1.M1-01, M1.pin_2
  N3: S1.M1-02, M1.pin_1
  N4: S1.M2-01, M2.pin_2
  N5: S1.M2-02, M2.pin_1
  N6: J1.pulse, Componente1.D11_PWM/MOSI
  N7: ULTRASONIDO.Trig, Componente1.D13/SCK
  N8: ULTRASONIDO.Echo, Componente1.D12/MISO
  N9: BAT1.V+, SWITCH.S
  N10: Componente1.D6_PWM, TCRT5000.D0
  N11: Componente1.D7, TCTR5000.D0

custom parts:
  H-Bridge with L298N: h-bridge
  TCRT5000 sensor module: breakout board with TCRT5000
